# Fritzing sketch meadow-sg90 (saved by Fritzing 0.9.6b)
breadboards: 1

parts:
  J1 = Basic Servo
  Mod1 = Meadow F7 Micro

nets:
  GND: J1.gnd, Mod1.GND
  VCC: J1.vcc, Mod1.3.3V
  N1: J1.pulse, Mod1.DO8
